// Logisim project ISA.circ as structural Verilog: 5 circuits, main circuit main
module main (
);

  ULA ula_1 ();  // open: seletor, A, B, Resultado
endmodule

module ULA (
  input  [2:0] seletor,
  input  [11:0] A,
  input  [11:0] B,
  output [11:0] Resultado
);

  wire [11:0] adder_1_out, and_1_out, not_1_out, or_1_out, subtractor_1_out;

  Adder #(.width(12)) adder_1 (.a(A), .b(B), .out(adder_1_out));  // open: cin, cout
  Subtractor #(.width(12)) subtractor_1 (.a(A), .b(B), .out(subtractor_1_out));  // open: bin, bout
  assign not_1_out = ~A;  // NOT_Gate not_1, 12 bits wide
  assign and_1_out = A & B;  // AND_Gate and_1, 12 bits wide
  assign or_1_out = A | B;  // OR_Gate or_1, 12 bits wide
  Multiplexer #(.select(3), .width(12)) multiplexer_1 (
    .in0(adder_1_out), .in1(subtractor_1_out), .in2(and_1_out), .in3(or_1_out), .in4(not_1_out),
    .out(Resultado), .sel(seletor));  // open: in5, in6, in7
endmodule

module BD (
  input  [11:0] WRITEDATA,
  input  [11:0] RS1,
  input  [11:0] RS2,
  input  regwrite,
  input  [2:0] RD
);

  wire R0, R1, R2, R3, R4, R5, R6, R7;
  wire [11:0] S0, S1, S2, S3, S4, S5, S6, S7;

  Register #(.width(12)) u_R0 (.D(WRITEDATA), .en(R0), .Q(S0));  // open: clk, clr
  Register #(.width(12)) u_R1 (.D(WRITEDATA), .en(R1), .Q(S1));  // open: clk, clr
  Register #(.width(12)) u_R2 (.D(WRITEDATA), .en(R2), .Q(S2));  // open: clk, clr
  Register #(.width(12)) u_R3 (.D(WRITEDATA), .en(R3), .Q(S3));  // open: clk, clr
  Demultiplexer #(.select(3)) demultiplexer_1 (
    .out0(R0), .out1(R1), .out2(R2), .out3(R3), .out4(R4), .out5(R5), .out6(R6), .out7(R7), .in(regwrite),
    .sel(RD));
  Register #(.width(12)) u_R4 (.D(WRITEDATA), .en(R4), .Q(S4));  // open: clk, clr
  Register #(.width(12)) u_R5 (.D(WRITEDATA), .en(R5), .Q(S5));  // open: clk, clr
  Register #(.width(12)) u_R6 (.D(WRITEDATA), .en(R6), .Q(S6));  // open: clk, clr
  Register #(.width(12)) u_R7 (.D(WRITEDATA), .en(R7), .Q(S7));  // open: clk, clr
  Multiplexer #(.select(3), .width(12)) multiplexer_1 (
    .in0(S0), .in1(S1), .in2(S2), .in3(S3), .in4(S4), .in5(S5), .in6(S6), .in7(S7), .out(RS1));  // open: sel
  Multiplexer #(.select(3), .width(12)) multiplexer_2 (
    .in0(S0), .in1(S1), .in2(S2), .in3(S3), .in4(S4), .in5(S5), .in6(S6), .in7(S7), .out(RS2));  // open: sel
endmodule

module PC (
  input  RESET
);

  wire clock_1_out;
  wire [9:0] adder_1_out, register_1_q;

  Clock clock_1 (.out(clock_1_out));
  Register #(.width(10)) register_1 (.D(adder_1_out), .en(1'b1), .clk(clock_1_out), .Q(register_1_q), .clr(RESET));
  Adder #(.width(10)) adder_1 (.a(register_1_q), .b(10'h1), .out(adder_1_out));  // open: cin, cout
endmodule

module MI (
);

  RAM #(.addrWidth(10), .dataWidth(10)) ram_1 ();  // open: addr, we, oe, clk, din, dout
endmodule
